// Logisim project Tp1.circ as structural Verilog: 1 circuit, main circuit main
module main (
  input  e0,
  input  e1,
  input  e2,
  input  in_4,
  input  in_5,
  input  [2:0] in_6,
  input  e0_2,
  input  e1_2,
  input  in_9,
  input  e7,
  input  e6,
  input  e5,
  input  e4,
  input  e3,
  input  e2_2,
  input  e1_3,
  input  e0_3,
  output s0,
  output s1,
  output s2,
  output s3,
  output s4,
  output s5,
  output s6,
  output s7,
  output [7:0] out_26,
  output out_27,
  output out_28,
  output s0_2,
  output s1_2,
  output s2_2
);

  wire and_1_out, and_2_out, and_3_out, and_4_out, not_1_out, not_2_out, not_3_out, not_4_out, not_5_out,
       not_6_out, not_7_out, not_8_out, not_9_out, not_10_out, not_11_out, not_12_out, not_13_out;

  not not_1 (not_1_out, e7);
  not not_2 (not_2_out, e0);
  not not_3 (not_3_out, e6);
  not not_4 (not_4_out, e5);
  not not_5 (not_5_out, e1);
  not not_6 (not_6_out, e4);
  not not_7 (not_7_out, e2);
  Decoder #(.select(3)) decoder_1 (
    .out0(out_26[0]), .out1(out_26[1]), .out2(out_26[2]), .out3(out_26[3]), .out4(out_26[4]),
    .out5(out_26[5]), .out6(out_26[6]), .out7(out_26[7]), .sel(in_6), .en(in_5));
  not not_8 (not_8_out, e3);
  and and_1 (and_1_out, e1_2, e1_2);
  and and_2 (and_2_out, e0_2, e0_2);
  and and_3 (and_3_out, in_9, e1_2);
  not not_9 (not_9_out, in_9);
  and and_4 (and_4_out, not_9_out, e0_2);
  not not_10 (not_10_out, e1_3);
  not not_11 (not_11_out, e2_2);
  and and_5 (s0, not_7_out, not_5_out, not_2_out);
  and and_6 (s1, e2, not_5_out, not_2_out);
  and and_7 (s2, not_7_out, e1, not_2_out);
  and and_8 (s3, e2, e1, not_2_out);
  and and_9 (s4, not_7_out, not_5_out, e0);
  and and_10 (s5, e2, not_5_out, e0);
  and and_11 (s6, not_7_out, e1, e0);
  and and_12 (s7, e2, e1, e0);
  not not_12 (not_12_out, and_1_out);
  not not_13 (not_13_out, e0_3);
  or or_1 (out_27, not_12_out, and_2_out);
  or or_2 (out_28, and_3_out, and_4_out);
  and and_13 (s0_2, e7, not_3_out, e5, not_6_out, e3, not_11_out, e1_3, not_13_out);
  and and_14 (s1_2, e7, e6, not_4_out, not_6_out, e3, e2_2, not_10_out, not_13_out);
  and and_15 (s2_2, e7, e6, e5, e4, not_8_out, not_11_out, not_10_out, not_13_out);
endmodule
