// Logisim project sequentiel.circ as structural Verilog: 16 circuits, main circuit main
module main (
  input  in_1,
  input  in_2,
  output out_3
);

  nand nand_1 (out_3, in_2, in_2);
endmodule

module Bistable (
  input  in_1,
  output Q,
  output nQ,
  output Q_2,
  output nQ_2
);

  wire not_1_out;

  not not_1 (not_1_out, in_1);
  not not_2 (in_1, not_1_out);
  not not_3 (Q, nQ);
  not not_4 (nQ, Q);
  nand nand_1 (Q_2, nQ_2, nQ_2);
  nand nand_2 (nQ_2, Q_2, Q_2);
endmodule

module RS_NAND (
  input  R,
  input  S,
  output Q,
  output nQ
);

  nand nand_1 (Q, R, nQ);
  nand nand_2 (nQ, Q, S);
endmodule

module RS_NOR (
  input  R,
  input  S,
  output Q,
  output nQ
);

  nor nor_1 (Q, R, nQ);
  nor nor_2 (nQ, Q, S);
endmodule

// LH
module Latch_NAND (
  input  D,
  input  C,
  output Q,
  output nQ
);

  wire nand_1_out, nand_2_out;

  nand nand_1 (nand_1_out, D, C);
  nand nand_2 (nand_2_out, nand_1_out, C);
  nand nand_3 (Q, nand_1_out, nQ);
  nand nand_4 (nQ, Q, nand_2_out);

  // Notes on the sheet:
  //   R
  //   S
endmodule

// LB
module Latch_NOR (
  input  D,
  input  C,
  output Q,
  output nQ
);

  wire nor_1_out, nor_2_out;

  nor nor_1 (nor_1_out, D, C);
  nor nor_2 (nor_2_out, nor_1_out, C);
  nor nor_3 (Q, nor_1_out, nQ);
  nor nor_4 (nQ, Q, nor_2_out);

  // Notes on the sheet:
  //   R
  //   S
endmodule

module \D_maître_esclave_NAND_NOR  (
  input  D,
  input  C,
  input  D_2,
  input  C_2,
  input  D_3,
  input  C_3,
  output Q,
  output nQ,
  output Q_2,
  output Q_3
);

  wire latch_nand_1_q, latch_nor_1_q, nand_1_out, nand_2_out, nand_3_out, nand_4_out, nor_1_out, nor_2_out;

  nand nand_1 (nand_1_out, D, C);
  Latch_NAND latch_nand_1 (.D(D_2), .C(C_2), .Q(latch_nand_1_q));  // open: nQ
  Latch_NOR latch_nor_1 (.D(D_3), .C(C_3), .Q(latch_nor_1_q));  // open: nQ
  nand nand_2 (nand_2_out, nand_1_out, C);
  Latch_NOR latch_nor_2 (.D(latch_nand_1_q), .C(C_2), .Q(Q_2));  // open: nQ
  Latch_NAND latch_nand_2 (.D(latch_nor_1_q), .C(C_3), .Q(Q_3));  // open: nQ
  nand nand_3 (nand_3_out, nand_1_out, nand_4_out);
  nand nand_4 (nand_4_out, nand_3_out, nand_2_out);
  nor nor_1 (nor_1_out, nand_3_out, C);
  nor nor_2 (nor_2_out, C, nand_4_out);
  nor nor_3 (Q, nor_1_out, nQ);
  nor nor_4 (nQ, Q, nor_2_out);

  // Notes on the sheet:
  //   Qm
  //   !Qm
endmodule

module D_edge_triggered (
  input  D,
  input  C,
  output nQ,
  output Q
);

  wire nand_1_out, nand_2_out, nand_3_out, nand_4_out;

  nand nand_1 (nand_1_out, nand_3_out, D);
  nand nand_2 (nand_2_out, nand_1_out, nand_4_out);
  nand nand_3 (nand_3_out, nand_1_out, C, nand_4_out);
  nand nand_4 (nand_4_out, C, nand_2_out);
  nand nand_5 (nQ, nand_3_out, Q);
  nand nand_6 (Q, nQ, nand_4_out);
endmodule

module Compteur_par_2 (
  output out_1
);

  wire clock_1_out, d_ff_1_qn;

  Clock clock_1 (.out(clock_1_out));
  D_Flip_Flop d_ff_1 (.clk(clock_1_out), .D(d_ff_1_qn), .Q(out_1), .Qn(d_ff_1_qn));  // open: preset, en, reset
endmodule

module Compteur_par_4 (
);

  wire clock_1_out, d_ff_1_q, d_ff_2_q, d_ff_2_qn, xor_1_out;

  Clock clock_1 (.out(clock_1_out));
  D_Flip_Flop d_ff_1 (.clk(clock_1_out), .D(xor_1_out), .Q(d_ff_1_q));  // open: Qn, preset, en, reset
  xor xor_1 (xor_1_out, d_ff_2_q, d_ff_1_q);
  D_Flip_Flop d_ff_2 (.clk(clock_1_out), .D(d_ff_2_qn), .Q(d_ff_2_q), .Qn(d_ff_2_qn));  // open: preset, en, reset
endmodule

module Registre_8_bits (
  input  [7:0] E,
  input  C,
  output [7:0] S
);

  D_edge_triggered d_edge_triggered_1 (.D(E[7]), .C(C), .Q(S[7]));  // open: nQ
  D_edge_triggered d_edge_triggered_2 (.D(E[6]), .C(C), .Q(S[6]));  // open: nQ
  D_edge_triggered d_edge_triggered_3 (.D(E[4]), .C(C), .Q(S[4]));  // open: nQ
  D_edge_triggered d_edge_triggered_4 (.D(E[5]), .C(C), .Q(S[5]));  // open: nQ
  D_edge_triggered d_edge_triggered_5 (.D(E[3]), .C(C), .Q(S[3]));  // open: nQ
  D_edge_triggered d_edge_triggered_6 (.D(E[2]), .C(C), .Q(S[2]));  // open: nQ
  D_edge_triggered d_edge_triggered_7 (.D(E[1]), .C(C), .Q(S[1]));  // open: nQ
  D_edge_triggered d_edge_triggered_8 (.D(E[0]), .C(C), .Q(S[0]));  // open: nQ
endmodule

module Banc_de_8_registres_8_bits (
  input  [2:0] rrA,
  input  [2:0] rrB,
  input  [2:0] rw,
  input  [7:0] wdata,
  input  C,
  input  W,
  output [7:0] rdataA,
  output [7:0] dataB,
  output [7:0] out_9,
  output [7:0] out_10,
  output [7:0] out_11,
  output [7:0] out_12,
  output [7:0] out_13,
  output [7:0] out_14,
  output [7:0] out_15,
  output [7:0] out_16
);

  wire and_1_out, and_2_out, and_3_out, and_4_out, and_5_out, and_6_out, and_7_out, and_8_out, and_9_out,
       decoder_1_out0, decoder_1_out1, decoder_1_out2, decoder_1_out3, decoder_1_out4, decoder_1_out5,
       decoder_1_out6, decoder_1_out7;

  Decoder #(.select(3)) decoder_1 (
    .out0(decoder_1_out0), .out1(decoder_1_out1), .out2(decoder_1_out2), .out3(decoder_1_out3),
    .out4(decoder_1_out4), .out5(decoder_1_out5), .out6(decoder_1_out6), .out7(decoder_1_out7), .sel(rw));  // open: en
  and and_1 (and_1_out, C, W);
  Registre_8_bits registre_8_bits_1 (.E(wdata), .C(and_2_out), .S(out_9));
  and and_2 (and_2_out, decoder_1_out0, and_1_out);
  Registre_8_bits registre_8_bits_2 (.E(wdata), .C(and_3_out), .S(out_10));
  and and_3 (and_3_out, decoder_1_out1, and_1_out);
  Registre_8_bits registre_8_bits_3 (.E(wdata), .C(and_4_out), .S(out_11));
  and and_4 (and_4_out, decoder_1_out2, and_1_out);
  Registre_8_bits registre_8_bits_4 (.E(wdata), .C(and_5_out), .S(out_12));
  and and_5 (and_5_out, decoder_1_out3, and_1_out);
  Registre_8_bits registre_8_bits_5 (.E(wdata), .C(and_6_out), .S(out_13));
  and and_6 (and_6_out, decoder_1_out4, and_1_out);
  Registre_8_bits registre_8_bits_6 (.E(wdata), .C(and_7_out), .S(out_14));
  and and_7 (and_7_out, decoder_1_out5, and_1_out);
  Registre_8_bits registre_8_bits_7 (.E(wdata), .C(and_8_out), .S(out_15));
  and and_8 (and_8_out, decoder_1_out6, and_1_out);
  Registre_8_bits registre_8_bits_8 (.E(wdata), .C(and_9_out), .S(out_16));
  and and_9 (and_9_out, decoder_1_out7, and_1_out);
  Multiplexer #(.select(3), .width(8)) multiplexer_1 (
    .in0(out_9), .in1(out_10), .in2(out_11), .in3(out_12), .in4(out_13), .in5(out_14), .in6(out_15),
    .in7(out_16), .out(rdataA), .sel(rrA));  // open: en
  Multiplexer #(.select(3), .width(8)) multiplexer_2 (
    .in0(out_9), .in1(out_10), .in2(out_11), .in3(out_12), .in4(out_13), .in5(out_14), .in6(out_15),
    .in7(out_16), .out(dataB), .sel(rrB));  // open: en
endmodule

module buffer (
  input  in_1,
  input  in_2,
  input  in_3,
  input  in_4,
  output out_5
);

  assign out_5 = in_1 ? in_2 : 1'bz;  // Controlled_Buffer controlled_buffer_1
  assign out_5 = in_4 ? in_3 : 1'bz;  // Controlled_Buffer controlled_buffer_2
endmodule

module RAM_4x2 (
  input  Din_1,
  input  Din_0,
  input  [1:0] in_3,
  input  WE,
  input  OE,
  output Dout_1,
  output Dout_0
);

  wire and_1_out, and_2_out, and_3_out, and_4_out, and_5_out, controlled_buffer_1_out,
       controlled_buffer_6_out, d_ff_1_q, d_ff_2_q, d_ff_3_q, d_ff_4_q, d_ff_5_q, d_ff_6_q, d_ff_7_q,
       d_ff_8_q, decoder_1_out0, decoder_1_out1, decoder_1_out2, decoder_1_out3, not_1_out;

  Decoder #(.select(2)) decoder_1 (
    .out0(decoder_1_out0), .out1(decoder_1_out1), .out2(decoder_1_out2), .out3(decoder_1_out3), .sel(in_3));  // open: en
  and and_1 (and_1_out, decoder_1_out0, WE);
  and and_2 (and_2_out, decoder_1_out1, WE);
  and and_3 (and_3_out, decoder_1_out2, WE);
  and and_4 (and_4_out, decoder_1_out3, WE);
  not not_1 (not_1_out, WE);
  D_Flip_Flop d_ff_1 (.clk(and_1_out), .D(Din_1), .Q(d_ff_1_q));  // open: Qn, preset, en, reset
  D_Flip_Flop d_ff_2 (.clk(and_2_out), .D(Din_1), .Q(d_ff_2_q));  // open: Qn, preset, en, reset
  D_Flip_Flop d_ff_3 (.clk(and_3_out), .D(Din_1), .Q(d_ff_3_q));  // open: Qn, preset, en, reset
  D_Flip_Flop d_ff_4 (.clk(and_4_out), .D(Din_1), .Q(d_ff_4_q));  // open: Qn, preset, en, reset
  and and_5 (and_5_out, not_1_out, OE);
  assign controlled_buffer_1_out = decoder_1_out0 ? d_ff_1_q : 1'bz;  // Controlled_Buffer controlled_buffer_1
  assign controlled_buffer_1_out = decoder_1_out1 ? d_ff_2_q : 1'bz;  // Controlled_Buffer controlled_buffer_2
  assign controlled_buffer_1_out = decoder_1_out2 ? d_ff_3_q : 1'bz;  // Controlled_Buffer controlled_buffer_3
  assign controlled_buffer_1_out = decoder_1_out3 ? d_ff_4_q : 1'bz;  // Controlled_Buffer controlled_buffer_4
  assign Dout_1 = and_5_out ? controlled_buffer_1_out : 1'bz;  // Controlled_Buffer controlled_buffer_5
  assign controlled_buffer_6_out = decoder_1_out0 ? d_ff_5_q : 1'bz;  // Controlled_Buffer controlled_buffer_6
  D_Flip_Flop d_ff_5 (.clk(and_1_out), .D(Din_0), .Q(d_ff_5_q));  // open: Qn, preset, en, reset
  D_Flip_Flop d_ff_6 (.clk(and_2_out), .D(Din_0), .Q(d_ff_6_q));  // open: Qn, preset, en, reset
  assign controlled_buffer_6_out = decoder_1_out1 ? d_ff_6_q : 1'bz;  // Controlled_Buffer controlled_buffer_7
  D_Flip_Flop d_ff_7 (.clk(and_3_out), .D(Din_0), .Q(d_ff_7_q));  // open: Qn, preset, en, reset
  assign controlled_buffer_6_out = decoder_1_out2 ? d_ff_7_q : 1'bz;  // Controlled_Buffer controlled_buffer_8
  assign controlled_buffer_6_out = decoder_1_out3 ? d_ff_8_q : 1'bz;  // Controlled_Buffer controlled_buffer_9
  D_Flip_Flop d_ff_8 (.clk(and_4_out), .D(Din_0), .Q(d_ff_8_q));  // open: Qn, preset, en, reset
  assign Dout_0 = and_5_out ? controlled_buffer_6_out : 1'bz;  // Controlled_Buffer controlled_buffer_10
endmodule

module cirAdams (
  input  D,
  input  C,
  output nQ,
  output Q
);

  wire nand_1_out, nand_2_out, nand_3_out, nand_4_out;

  nand nand_1 (nand_1_out, nand_3_out, D);
  nand nand_2 (nand_2_out, nand_1_out, nand_4_out);
  nand nand_3 (nand_3_out, nand_1_out, C, nand_4_out);
  nand nand_4 (nand_4_out, C, nand_2_out);
  nand nand_5 (nQ, nand_3_out, Q);
  nand nand_6 (Q, nQ, nand_4_out);
endmodule

module tp3question1 (
  input  in_1,
  input  constant,
  input  in_3,
  input  in_4,
  input  in_5,
  input  in_6,
  input  [3:0] in_7,
  output out_8,
  output out_9,
  output out_10,
  output [3:0] out_11
);

  wire ciradams_1_q, clock_1_out, clock_2_out, clock_3_out, d_ff_1_q, d_ff_2_q, d_ff_3_q, d_ff_4_q, d_ff_6_q,
       d_ff_7_q, or_1_out, undriven;

  Clock clock_1 (.out(clock_1_out));
  Clock clock_2 (.out(clock_2_out));
  or or_1 (or_1_out, in_6, d_ff_7_q);
  Clock clock_3 (.out(clock_3_out));
  D_Flip_Flop d_ff_1 (.clk(clock_2_out), .D(or_1_out), .Q(d_ff_1_q), .reset(in_5));  // open: Qn, preset, en
  LED led_1 (.in(d_ff_1_q));
  Register #(.width(1)) register_1 (.D(in_7[3]), .Q(out_11[3]), .clk(clock_2_out));  // open: en, clr
  D_Flip_Flop d_ff_2 (.clk(clock_2_out), .D(d_ff_1_q), .Q(d_ff_2_q), .reset(in_5));  // open: Qn, preset, en
  LED led_2 (.in(d_ff_2_q));
  Register #(.width(1)) register_2 (.D(in_7[2]), .Q(out_11[2]), .clk(clock_2_out));  // open: en, clr
  cirAdams ciradams_1 (.D(clock_3_out), .C(constant), .Q(ciradams_1_q));  // open: nQ
  D_Flip_Flop d_ff_3 (.clk(clock_1_out), .D(in_3), .Q(d_ff_3_q), .reset(in_4));  // open: Qn, preset, en
  Register #(.width(1)) register_3 (.D(in_7[1]), .Q(out_11[1]), .clk(clock_2_out));  // open: en, clr
  D_Flip_Flop d_ff_4 (.clk(clock_2_out), .D(d_ff_2_q), .Q(d_ff_4_q), .reset(in_5));  // open: Qn, preset, en
  LED led_3 (.in(d_ff_4_q));
  Register #(.width(1)) register_4 (.D(in_7[0]), .Q(out_11[0]), .clk(clock_2_out));  // open: en, clr
  cirAdams ciradams_2 (.D(undriven), .C(constant), .nQ(out_8), .Q(out_9));
  D_Flip_Flop d_ff_5 (.clk(clock_1_out), .D(d_ff_3_q), .Q(out_10), .reset(in_4));  // open: Qn, preset, en
  D_Flip_Flop d_ff_6 (.clk(clock_2_out), .D(d_ff_4_q), .Q(d_ff_6_q), .reset(in_5));  // open: Qn, preset, en
  LED led_4 (.in(d_ff_6_q));
  D_Flip_Flop d_ff_7 (.clk(clock_2_out), .D(d_ff_6_q), .Q(d_ff_7_q), .reset(in_5));  // open: Qn, preset, en
  LED led_5 (.in(d_ff_7_q));
endmodule
