// Logisim project tp2_aluetu.circ as structural Verilog: 4 circuits, main circuit ALU
module ALU (
  input  [15:0] Input1,
  input  [15:0] Input2,
  input  [15:0] Cst,
  input  e1,
  input  [1:0] e2,
  output [15:0] Output
);

  wire [15:0] adder_1_out, and_1_out, multiplexer_1_out, not_1_out;

  Multiplexer #(.width(16), .enable("false")) multiplexer_1 (
    .in0(Input2), .in1(Cst), .out(multiplexer_1_out), .sel(e1));
  Adder #(.width(16)) adder_1 (.a(multiplexer_1_out), .b(Input1), .out(adder_1_out));  // open: cin, cout
  assign and_1_out = Input1 & multiplexer_1_out;  // AND_Gate and_1, 16 bits wide
  Multiplexer #(.select(2), .width(16), .enable("false")) multiplexer_2 (
    .in0(adder_1_out), .in1(and_1_out), .in2(not_1_out), .out(Output), .sel(e2));  // open: in3
  assign not_1_out = ~Input1;  // NOT_Gate not_1, 16 bits wide
endmodule

module ALU_test (
  input  e1,
  input  [1:0] e2
);

  wire [15:0] alu_1_output;

  ALU alu_1 (.e1(e1), .e2(e2), .Output(alu_1_output), .Input1(16'h1234), .Input2(16'h4567), .Cst({16{1'b1}}));
  // Probe on alu_1_output

  // Notes on the sheet:
  //   Cst
  //   Input1
  //   Input2
endmodule

module NZP (
  input  in_1,
  input  in_2,
  input  in_3,
  input  in_4,
  input  in_5,
  input  in_6,
  input  in_7,
  input  in_8,
  input  in_9,
  input  in_10,
  input  in_11,
  input  in_12,
  input  in_13,
  input  in_14,
  input  in_15,
  input  in_16,
  input  [15:0] in_17,
  input  in_18,
  output z,
  output p,
  output n
);

  nor nor_1 (z, in_17[0], in_17[1], in_17[2], in_17[3], in_17[4], in_17[5], in_17[6], in_17[7], in_17[8], in_17[9], in_17[10], in_17[11], in_17[12], in_17[13], in_17[14], in_17[15]);
  nor nor_2 (p, z, in_17[15]);

  assign n = in_17[15];

  // Notes on the sheet:
  //   RES
endmodule

module Ext8vers16 (
  input  [7:0] in_1,
  input  [7:0] in_2,
  output [15:0] out_3,
  output [15:0] out_4
);

  assign out_4 = {{8{in_2[7]}}, in_2};  // Bit_Extender bit_extender_1

  assign out_3 = {{9{in_1[7]}}, in_1[6:0]};
endmodule
