// Logisim project tp2_pgcdetu.circ as structural Verilog: 1 circuit, main circuit gcd
module gcd (
  input  [7:0] x_input,
  input  [7:0] y_input,
  input  RESET
);

  wire button_1_out;
  wire [7:0] multiplexer_1_out, multiplexer_2_out, subtractor_1_out, subtractor_2_out, X_q, Y_q;

  // Probe on x_input
  // Probe on y_input
  Multiplexer #(.width(8), .enable("false")) multiplexer_1 (
    .in0(subtractor_1_out), .in1(x_input), .out(multiplexer_1_out));  // open: sel
  Multiplexer #(.width(8), .enable("false")) multiplexer_2 (
    .in0(subtractor_2_out), .in1(y_input), .out(multiplexer_2_out));  // open: sel
  Register X (.D(multiplexer_1_out), .Q(X_q), .clk(button_1_out));  // open: en, clr
  Register Y (.D(multiplexer_2_out), .Q(Y_q), .clk(button_1_out));  // open: en, clr
  Button button_1 (.out(button_1_out));
  // Probe on Y_q
  // Probe on X_q
  Subtractor subtractor_1 (.a(X_q), .b(Y_q), .out(subtractor_1_out));  // open: bin, bout
  Subtractor subtractor_2 (.a(Y_q), .b(X_q), .out(subtractor_2_out));  // open: bin, bout

  // Notes on the sheet:
  //   Circuit dédié au calcul de PGCD de deux nombres positifs
  //   CLOCK
  //   X - Y
  //   Y - X
endmodule
